# Fritzing sketch Projeto3 (saved by Fritzing 0.9.5d)
circuit board: 8.46667cm x 5.64444cm
breadboards: 1

parts:
  Part1 = Arduino Uno (Rev3)
  S1 = Pushbutton [package="[SMD]"]
  R1 = Resistor [tolerance=±5% resistance=220 package=THT]
  R2 = Resistor [tolerance=±5% resistance=10k package=THT]
  LED1 = LED - 5mm [color="Red (633nm)" package="5 mm [THT]"]

nets:
  N1: Part1.D13/SCK, LED1.anode
  N2: Part1.GND, R1.Pin_1, R2.Pin_1
  N3: Part1.D2, S1.Pin_1, S1.Pin_2, R2.Pin_0
  N4: Part1.5V, S1.Pin_3, S1.Pin_4, R1.Pin_0, LED1.cathode
