# Fritzing sketch Projeto5 (saved by Fritzing 0.9.5d)
circuit board: 8.46667cm x 5.64444cm
breadboards: 1

parts:
  Part1 = Arduino Uno (Rev3)
  R1 = Rotary Potentiometer (Small) [maximum_resistance=100kΩ package=THT]
  R2 = Resistor [tolerance=±5% resistance=220 package=THT]
  LED1 = LED - 5mm [color="Red (633nm)" package="5 mm [THT]"]

nets:
  N1: Part1.A1, R1.wiper
  N2: Part1.D9_PWM, LED1.anode
  N3: Part1.5V, R1.leg2
  N4: Part1.GND, R1.leg1, R2.Pin_1
  N5: R2.Pin_0, LED1.cathode
