# Fritzing sketch Projeto7 (saved by Fritzing 0.9.5d)
circuit board: 8.46667cm x 5.64444cm
breadboards: 1

parts:
  Part1 = Arduino Uno (Rev3)
  LED1 = RGB LED - (4 legs) [package="5 mm [THT]"]
  R1 = Resistor [tolerance=±5% resistance=220 package=THT]
  R2 = Resistor [tolerance=±5% resistance=220 package=THT]
  R3 = Resistor [tolerance=±5% resistance=220 package=THT]

nets:
  N1: Part1.D9_PWM, Part1.D10_PWM/SS, Part1.D11_PWM/MOSI, R1.Pin_0, R2.Pin_0, R3.Pin_0
  N2: Part1.GND, LED1.common_anode
  N3: LED1.red_cathode, LED1.green_cathode, LED1.blue_cathode, R1.Pin_1, R2.Pin_1, R3.Pin_1
